// Logisim project Procesador Monociclo 16 bits.circ as structural Verilog: 7 circuits, main circuit main
module main (
);

  wire ALU, and_1_out, clk, COND, JUMP, MEMREAD, MEMTOREG, MEMWRITE, or_1_out, REGWRITE, SUMAI;
  wire [1:0] CMPOP, multiplexer_4_out;
  wire [2:0] ALUOP, multiplexer_2_out, RD, RS1, RS2;
  wire [3:2] OPCODE;
  wire [7:0] adder_1_out, adder_2_out, ExtSign_inm__8, multiplexer_1_out, PC_q;
  wire [15:0] alu_1_aluout, BR_RS1, BR_RS2, extsign_1_extsigno_inm__16, memdata_1_dataout, multiplexer_3_out,
       multiplexer_5_out, multiplexer_6_out;

  Clock clock_1 (.out(clk));
  Register PC (.D(multiplexer_1_out), .en(1'b1), .Q(PC_q), .clk(clk));  // open: clr
  // Probe on {OPCODE, CMPOP, RD, RS1, RS2, ALUOP}
  MEMINST meminst_1 (.ADDR(PC_q), .INST({OPCODE, CMPOP, RD, RS1, RS2, ALUOP}));
  ExtSign extsign_1 (
    .INST({RD, RS1, RS2, ALUOP}), .ExtSigno_inm__16(extsign_1_extsigno_inm__16),
    .ExtSigno_inm__8(ExtSign_inm__8));
  Adder adder_1 (.a(8'h1), .b(PC_q), .out(adder_1_out));  // open: cin, cout
  Adder adder_2 (.a(PC_q), .b(ExtSign_inm__8), .out(adder_2_out));  // open: cin, cout
  UC uc_1 (
    .OPCODE({OPCODE, CMPOP}), .MEMREAD(MEMREAD), .REGWRITE(REGWRITE), .ALU(ALU), .MEMWRITE(MEMWRITE),
    .MEMTOREG(MEMTOREG), .JUMP(JUMP), .SUMAI(SUMAI));
  and and_1 (and_1_out, JUMP, COND);
  Multiplexer #(.width(8), .enable("false")) multiplexer_1 (
    .in0(adder_1_out), .in1(adder_2_out), .out(multiplexer_1_out), .sel(and_1_out));
  or or_1 (or_1_out, JUMP, MEMWRITE);
  Multiplexer #(.width(3), .enable("false")) multiplexer_2 (
    .in0(RS2), .in1(RD), .out(multiplexer_2_out), .sel(or_1_out));
  BR br_1 (
    .RS1(RS1), .RS2(multiplexer_2_out), .RD(RD), .C(multiplexer_5_out), .A(BR_RS1), .B(BR_RS2),
    .wr(REGWRITE), .clk(clk));  // open: reset
  Multiplexer #(.width(16), .enable("false")) multiplexer_3 (
    .in0(BR_RS2), .in1(extsign_1_extsigno_inm__16), .out(multiplexer_3_out), .sel(SUMAI));
  Multiplexer #(.width(2), .enable("false")) multiplexer_4 (
    .in0(2'b00), .in1(ALUOP[1:0]), .out(multiplexer_4_out), .sel(ALU));
  Multiplexer #(.width(16), .enable("false")) multiplexer_5 (
    .in0(alu_1_aluout), .in1(memdata_1_dataout), .out(multiplexer_5_out), .sel(MEMTOREG));
  ALU alu_1 (
    .A(BR_RS1), .B(multiplexer_3_out), .ALUOUT(alu_1_aluout), .Op(multiplexer_4_out), .JUMPOUT(COND),
    .Op_2(CMPOP));
  Multiplexer #(.width(16), .enable("false")) multiplexer_6 (
    .in0(alu_1_aluout), .in1(BR_RS2), .out(multiplexer_6_out), .sel(MEMWRITE));
  MEMDATA memdata_1 (
    .ADDR(multiplexer_6_out), .DATAIN(BR_RS1), .DATAOUT(memdata_1_dataout), .wr(MEMWRITE), .clk(clk),
    .read(MEMREAD));  // open: reset

  // Other names for the same wires on the sheet: OPCODE[1:0] = CMPOP
endmodule

module BR (
  input  wr,
  input  clk,
  input  reset,
  input  [2:0] RS1,
  input  [2:0] RS2,
  input  [2:0] RD,
  input  [15:0] C,
  output [15:0] A,
  output [15:0] B
);

  wire decoder_1_out1, decoder_1_out2, decoder_1_out3, decoder_1_out4, decoder_1_out5, decoder_1_out6,
       decoder_1_out7;
  wire [15:0] ax_q, bx_q, cx_q, dx_q, ex_q, fx_q, gx_q;

  Decoder #(.select(3), .disabled(0)) decoder_1 (
    .out1(decoder_1_out1), .out2(decoder_1_out2), .out3(decoder_1_out3), .out4(decoder_1_out4),
    .out5(decoder_1_out5), .out6(decoder_1_out6), .out7(decoder_1_out7), .sel(RD), .en(wr));  // open: out0
  Register #(.width(16)) ax (.D(C), .en(decoder_1_out1), .Q(ax_q), .clk(clk), .clr(reset));
  Register #(.width(16)) bx (.D(C), .en(decoder_1_out2), .Q(bx_q), .clk(clk), .clr(reset));
  Register #(.width(16)) cx (.D(C), .en(decoder_1_out3), .Q(cx_q), .clk(clk), .clr(reset));
  Register #(.width(16)) dx (.D(C), .en(decoder_1_out4), .Q(dx_q), .clk(clk), .clr(reset));
  Register #(.width(16)) ex (.D(C), .en(decoder_1_out5), .Q(ex_q), .clk(clk), .clr(reset));
  Register #(.width(16)) fx (.D(C), .en(decoder_1_out6), .Q(fx_q), .clk(clk), .clr(reset));
  Register #(.width(16)) gx (.D(C), .en(decoder_1_out7), .Q(gx_q), .clk(clk), .clr(reset));
  Multiplexer #(.select(3), .width(16), .enable("false")) multiplexer_1 (
    .in0({16{1'b0}}), .in1(ax_q), .in2(bx_q), .in3(cx_q), .in4(dx_q), .in5(ex_q), .in6(fx_q), .in7(gx_q),
    .out(A), .sel(RS1));
  Multiplexer #(.select(3), .width(16), .enable("false")) multiplexer_2 (
    .in0({16{1'b0}}), .in1(ax_q), .in2(bx_q), .in3(cx_q), .in4(dx_q), .in5(ex_q), .in6(fx_q), .in7(gx_q),
    .out(B), .sel(RS2));

  // Notes on the sheet:
  //   r0
endmodule

module ALU (
  input  [1:0] Op,
  input  [15:0] A,
  input  [15:0] B,
  input  [1:0] Op_2,
  output [15:0] ALUOUT,
  output JUMPOUT
);

  wire comparator_1_eq, comparator_1_lt, or_2_out, undriven;
  wire [15:0] adder_1_out, and_1_out, or_1_out, subtractor_1_out;

  Adder #(.width(16)) adder_1 (.a(A), .b(B), .out(adder_1_out));  // open: cin, cout
  Subtractor #(.width(16)) subtractor_1 (.a(A), .b(B), .out(subtractor_1_out));  // open: bin, bout
  assign and_1_out = A & B;  // AND_Gate and_1, 16 bits wide
  assign or_1_out = A | B;  // OR_Gate or_1, 16 bits wide
  Comparator #(.width(16)) comparator_1 (.a(B), .b(A), .eq(comparator_1_eq), .lt(comparator_1_lt));  // open: gt
  or or_2 (or_2_out, comparator_1_eq, comparator_1_lt);
  Multiplexer #(.select(2), .width(16), .enable("false")) multiplexer_1 (
    .in0(adder_1_out), .in1(subtractor_1_out), .in2(and_1_out), .in3(or_1_out), .out(ALUOUT), .sel(Op));
  Multiplexer #(.select(2), .enable("false")) multiplexer_2 (
    .in0(undriven), .in1(comparator_1_eq), .in2(comparator_1_lt), .in3(or_2_out), .out(JUMPOUT), .sel(Op_2));
endmodule

module MEMDATA (
  input  [15:0] ADDR,
  input  [15:0] DATAIN,
  input  wr,
  input  reset,
  input  read,
  input  clk,
  output [15:0] DATAOUT
);

  wire undriven;

  RAM #(.addrWidth(16), .dataWidth(16), .bus("separate")) ram_1 (
    .addr(ADDR), .din(DATAIN), .data(DATAOUT), .str(wr), .sel(undriven), .clk(clk), .ld(read), .clr(reset));
endmodule

module MEMINST (
  input  [7:0] ADDR,
  output [15:0] INST
);

  ROM #(.dataWidth(16)) rom_1 (.addr(ADDR), .data(INST));  // open: sel

  // Notes on the sheet:
  //   contents of rom_1 (hex, n*v repeats v):
  //   0 2244 2482 1650 1851 5502 0 3aa0 4540
endmodule

module UC (
  input  [3:0] OPCODE,
  output ALU,
  output SUMAI,
  output REGWRITE,
  output MEMREAD,
  output MEMTOREG,
  output MEMWRITE,
  output JUMP
);

  wire IGUAL_out, MENIG_out, MENOR_out;

  // AND_Gate NOP has open pins: in0=OPCODE[3], in1=OPCODE[2], in2=OPCODE[1], in3=OPCODE[0], out=open
  and u_ALU (ALU, ~OPCODE[3], ~OPCODE[2], ~OPCODE[1], OPCODE[0]);  // AND_Gate
  and u_SUMAI (SUMAI, ~OPCODE[3], ~OPCODE[2], OPCODE[1], ~OPCODE[0]);  // AND_Gate
  and CAR (MEMREAD, ~OPCODE[3], ~OPCODE[2], OPCODE[1], OPCODE[0]);  // AND_Gate
  and ALM (MEMWRITE, ~OPCODE[3], OPCODE[2], ~OPCODE[1], ~OPCODE[0]);  // AND_Gate
  and IGUAL (IGUAL_out, ~OPCODE[3], OPCODE[2], ~OPCODE[1], OPCODE[0]);  // AND_Gate
  and MENOR (MENOR_out, ~OPCODE[3], OPCODE[2], OPCODE[1], ~OPCODE[0]);  // AND_Gate
  and MENIG (MENIG_out, ~OPCODE[3], OPCODE[2], OPCODE[1], OPCODE[0]);  // AND_Gate
  or or_1 (REGWRITE, ALU, SUMAI, MEMREAD);
  or or_2 (JUMP, IGUAL_out, MENOR_out, MENIG_out);

  assign MEMTOREG = MEMREAD;
endmodule

module ExtSign (
  input  [11:0] INST,
  output [15:0] ExtSigno_inm__16,
  output [7:0] ExtSigno_inm__8
);

  assign ExtSigno_inm__16 = {{10{INST[5]}}, INST[5:0]};  // Bit_Extender bit_extender_1
  assign ExtSigno_inm__8 = {{2{INST[5]}}, INST[5:0]};  // Bit_Extender bit_extender_2
endmodule
